// Logisim project project2.circ as structural Verilog: 4 circuits, main circuit main
module Register_File (
  input  Clock,
  input  [1:0] WriteReg,
  input  RegWrite,
  input  [7:0] RegDataW,
  input  [1:0] ReadReg1,
  input  [1:0] ReadReg2,
  output [7:0] RegData1,
  output [7:0] RegData2
);

  wire and_1_out, and_2_out, and_3_out, and_4_out, decoder_1_out0, decoder_1_out1, decoder_1_out2,
       decoder_1_out3;
  wire [7:0] r0_q, r1_q, r2_q, r3_q;

  Decoder #(.select(2)) decoder_1 (
    .out0(decoder_1_out0), .out1(decoder_1_out1), .out2(decoder_1_out2), .out3(decoder_1_out3), .sel(WriteReg));  // open: en
  and and_1 (and_1_out, RegWrite, decoder_1_out0);
  and and_2 (and_2_out, RegWrite, decoder_1_out1);
  and and_3 (and_3_out, RegWrite, decoder_1_out2);
  and and_4 (and_4_out, RegWrite, decoder_1_out3);
  Register r0 (.D(RegDataW), .en(and_1_out), .clk(Clock), .Q(r0_q));  // open: clr
  Register r1 (.D(RegDataW), .en(and_2_out), .clk(Clock), .Q(r1_q));  // open: clr
  Register r2 (.D(RegDataW), .en(and_3_out), .clk(Clock), .Q(r2_q));  // open: clr
  Register r3 (.D(RegDataW), .en(and_4_out), .clk(Clock), .Q(r3_q));  // open: clr
  Multiplexer #(.select(2), .width(8)) multiplexer_1 (
    .in0(r0_q), .in1(r1_q), .in2(r2_q), .in3(r3_q), .out(RegData1), .sel(ReadReg1));
  Multiplexer #(.select(2), .width(8)) multiplexer_2 (
    .in0(r0_q), .in1(r1_q), .in2(r2_q), .in3(r3_q), .out(RegData2), .sel(ReadReg2));
endmodule

module ALU (
  input  [7:0] input_a,
  input  [7:0] input_b,
  input  op,
  output [7:0] out_put,
  output C
);

  wire [7:0] multiplexer_1_out, not_1_out;

  assign not_1_out = ~input_b;  // NOT_Gate not_1, 8 bits wide
  Multiplexer #(.width(8)) multiplexer_1 (.in0(input_b), .in1(not_1_out), .out(multiplexer_1_out), .sel(op));
  Arithmetic_Unit arithmetic_unit_1 (
    .cin(op), .inputA(input_a), .inputB(multiplexer_1_out), .outpu_t(out_put), .cout(C));

  // Notes on the sheet:
  //   ADD 00
  //   SUB 01
endmodule

module Arithmetic_Unit (
  input  cin,
  input  [7:0] inputA,
  input  [7:0] inputB,
  output [7:0] outpu_t,
  output cout
);

  wire adder_1_cout, adder_2_cout, adder_3_cout, adder_4_cout, adder_5_cout, adder_6_cout, adder_7_cout;

  Adder #(.width(1)) adder_1 (.a(inputA[0]), .b(inputB[0]), .out(outpu_t[0]), .cin(cin), .cout(adder_1_cout));
  Adder #(.width(1)) adder_2 (.a(inputA[1]), .b(inputB[1]), .out(outpu_t[1]), .cin(adder_1_cout), .cout(adder_2_cout));
  Adder #(.width(1)) adder_3 (.a(inputA[2]), .b(inputB[2]), .out(outpu_t[2]), .cin(adder_2_cout), .cout(adder_3_cout));
  Adder #(.width(1)) adder_4 (.a(inputA[3]), .b(inputB[3]), .out(outpu_t[3]), .cin(adder_3_cout), .cout(adder_4_cout));
  Adder #(.width(1)) adder_5 (.a(inputA[4]), .b(inputB[4]), .out(outpu_t[4]), .cin(adder_4_cout), .cout(adder_5_cout));
  Adder #(.width(1)) adder_6 (.a(inputA[5]), .b(inputB[5]), .out(outpu_t[5]), .cin(adder_5_cout), .cout(adder_6_cout));
  Adder #(.width(1)) adder_7 (.a(inputA[6]), .b(inputB[6]), .out(outpu_t[6]), .cin(adder_6_cout), .cout(adder_7_cout));
  Adder #(.width(1)) adder_8 (.a(inputA[7]), .b(inputB[7]), .out(outpu_t[7]), .cin(adder_7_cout), .cout(cout));
endmodule

module main (
  output [7:0] IMM,
  output Math,
  output MemRead,
  output useImm,
  output MemWrite
);

  wire clock_1_out, clock_2_out;
  wire [1:0] multiplexer_1_out;
  wire [7:0] adder_1_out, alu_1_out_put, multiplexer_2_out, multiplexer_3_out, multiplexer_4_out, ram_2_dout,
       register_1_q, register_file_1_regdata1, register_file_1_regdata2;
  wire [15:6] ram_1_dout;

  Clock clock_1 (.out(clock_1_out));
  Register register_1 (.D(adder_1_out), .en(1'b1), .clk(clock_1_out), .Q(register_1_q));  // open: clr
  RAM #(.dataWidth(16), .enables("line")) ram_1 (
    .addr(register_1_q), .we(1'b0), .clk(clock_1_out),
    .dout({ram_1_dout[15:13], MemRead, MemWrite, useImm, ram_1_dout[9:6], IMM[5:0]}));  // open: din
  Adder adder_1 (.a(register_1_q), .b(8'h1), .out(adder_1_out));  // open: cin, cout
  and and_1 (Math, ram_1_dout[14], ram_1_dout[13]);
  Multiplexer #(.width(2)) multiplexer_1 (
    .in0(ram_1_dout[7:6]), .in1(ram_1_dout[9:8]), .out(multiplexer_1_out), .sel(ram_1_dout[15]));
  Register_File register_file_1 (
    .Clock(clock_1_out), .WriteReg(ram_1_dout[9:8]), .RegWrite(ram_1_dout[13]), .RegDataW(multiplexer_4_out),
    .ReadReg1(multiplexer_1_out), .ReadReg2(IMM[5:4]), .RegData1(register_file_1_regdata1),
    .RegData2(register_file_1_regdata2));
  Multiplexer #(.width(8)) multiplexer_2 (
    .in0(register_file_1_regdata2), .in1({2'b00, IMM[5:0]}), .out(multiplexer_2_out), .sel(useImm));
  ALU alu_1 (
    .input_a(register_file_1_regdata1), .input_b(multiplexer_2_out), .op(Math), .out_put(alu_1_out_put));  // open: C
  Clock clock_2 (.out(clock_2_out));
  Multiplexer #(.width(8)) multiplexer_3 (
    .in0(alu_1_out_put), .out(multiplexer_3_out), .sel(ram_1_dout[15]));  // open: in1
  RAM #(.enables("line")) ram_2 (
    .addr(multiplexer_2_out), .we(MemWrite), .clk(clock_2_out), .din(register_file_1_regdata1),
    .dout(ram_2_dout));
  Hex_Digit_Display hex_digit_display_1 (.value(multiplexer_3_out[7:4]));  // open: dp
  Hex_Digit_Display hex_digit_display_2 (.value(multiplexer_3_out[3:0]));  // open: dp
  Multiplexer #(.width(8)) multiplexer_4 (
    .in0(alu_1_out_put), .in1(ram_2_dout), .out(multiplexer_4_out), .sel(MemRead));

  assign IMM[7:6] = 2'b00;

  // Notes on the sheet:
  //   Next PC
  //   Jimmy Zhang & Barnatt Wu
  //   Factory CPU
  //   I pledge my honor that I have abided by the Stevens Honor System.
  //   0 = ADD
  //   1 = SUB
endmodule
